# Fritzing sketch power (saved by Fritzing 0.9.0b)
stripboards: 1

parts:
  J1 = Screw terminal - 2 pins [package=THT]
  J2 = Screw terminal - 2 pins [package=THT]  # not connected
  J3 = Screw terminal - 2 pins [package=THT]
  D1 = Rectifier Diode [part_number=1N4001 package="300 mil [THT]"]  # not connected
  C1 = Electrolytic Capacitor [capacitance=1µF package="100 mil [THT, electrolytic]"]
  3_3v_Regulator = mystery part, 3 pins [chip_label=?]
  LDR_1M_dark_->_8k_light = Photocell (LDR) [package=THT]
  VCC1 = 4 x AAA Battery Mount
  D2 = SOLAR-IXYS [package=solarbit-12x1]  # not connected
  Bypass_PNP_switch = Screw terminal - 2 pins [package=THT]
  Pull_up = Resistor [tolerance=±5% resistance=33k package=THT]
  BC327_PNP = PNP-Transistor [package="TO92 [THT]"]

nets:
  N1: J1.pin1, C1.+, 3_3v_Regulator.pin1
  N2: J1.pin2, J3.pin1, C1.-, 3_3v_Regulator.pin2, LDR_1M_dark_->_8k_light.pin_1, VCC1.-
  N3: 3_3v_Regulator.pin3, Bypass_PNP_switch.pin2, BC327_PNP.C
  N4: LDR_1M_dark_->_8k_light.pin_0, Pull_up.Pin_0, BC327_PNP.B
  N5: VCC1.+, Bypass_PNP_switch.pin1, Pull_up.Pin_1, BC327_PNP.E

notes:
  mA
  V
